// Logisim project CPU.circ as structural Verilog: 10 circuits, main circuit main
module RF (
  input  clk,
  input  rst,
  input  we,
  input  [4:0] A1,
  input  [4:0] A2,
  input  [4:0] A3,
  input  [31:0] WD,
  output [31:0] RD1,
  output [31:0] RD2
);

  wire [31:0] i0, i1, i2, i3, i4, i5, i6, i7, i8, i9, i10, i11, i12, i13, i14, i15, i16, i17, i18, i19, i20,
       i21, i22, i23, i24, i25, i26, i27, i28, i29, i30, i31, o0, o1, o2, o3, o4, o5, o6, o7, o8, o9, o10,
       o11, o12, o13, o14, o15, o16, o17, o18, o19, o20, o21, o22, o23, o24, o25, o26, o27, o28, o29, o30,
       o31;

  Demultiplexer #(.select(5), .width(32), .tristate("true")) demultiplexer_1 (
    .out0(i0), .out1(i1), .out2(i2), .out3(i3), .out4(i4), .out5(i5), .out6(i6), .out7(i7), .out8(i8),
    .out9(i9), .out10(i10), .out11(i11), .out12(i12), .out13(i13), .out14(i14), .out15(i15), .out16(i16),
    .out17(i17), .out18(i18), .out19(i19), .out20(i20), .out21(i21), .out22(i22), .out23(i23), .out24(i24),
    .out25(i25), .out26(i26), .out27(i27), .out28(i28), .out29(i29), .out30(i30), .out31(i31), .in(WD),
    .sel(A3), .en(we));
  Register #(.width(32)) _0 (.D(i0), .en(1'b0), .Q(o0), .clk(clk), .clr(rst));
  Register #(.width(32)) _4 (.D(i4), .en(we), .Q(o4), .clk(clk), .clr(rst));
  Register #(.width(32)) _8 (.D(i8), .en(we), .Q(o8), .clk(clk), .clr(rst));
  Register #(.width(32)) _12 (.D(i12), .en(we), .Q(o12), .clk(clk), .clr(rst));
  Register #(.width(32)) _16 (.D(i16), .en(we), .Q(o16), .clk(clk), .clr(rst));
  Register #(.width(32)) _20 (.D(i20), .en(we), .Q(o20), .clk(clk), .clr(rst));
  Register #(.width(32)) _24 (.D(i24), .en(we), .Q(o24), .clk(clk), .clr(rst));
  Register #(.width(32)) _28 (.D(i28), .en(we), .Q(o28), .clk(clk), .clr(rst));
  Register #(.width(32)) _1 (.D(i1), .en(we), .Q(o1), .clk(clk), .clr(rst));
  Register #(.width(32)) _5 (.D(i5), .en(we), .Q(o5), .clk(clk), .clr(rst));
  Register #(.width(32)) _9 (.D(i9), .en(we), .Q(o9), .clk(clk), .clr(rst));
  Register #(.width(32)) _13 (.D(i13), .en(we), .Q(o13), .clk(clk), .clr(rst));
  Register #(.width(32)) _17 (.D(i17), .en(we), .Q(o17), .clk(clk), .clr(rst));
  Register #(.width(32)) _21 (.D(i21), .en(we), .Q(o21), .clk(clk), .clr(rst));
  Register #(.width(32)) _25 (.D(i25), .en(we), .Q(o25), .clk(clk), .clr(rst));
  Register #(.width(32)) _29 (.D(i29), .en(we), .Q(o29), .clk(clk), .clr(rst));
  Register #(.width(32)) _2 (.D(i2), .en(we), .Q(o2), .clk(clk), .clr(rst));
  Register #(.width(32)) _6 (.D(i6), .en(we), .Q(o6), .clk(clk), .clr(rst));
  Register #(.width(32)) _10 (.D(i10), .en(we), .Q(o10), .clk(clk), .clr(rst));
  Register #(.width(32)) _14 (.D(i14), .en(we), .Q(o14), .clk(clk), .clr(rst));
  Register #(.width(32)) _18 (.D(i18), .en(we), .Q(o18), .clk(clk), .clr(rst));
  Register #(.width(32)) _22 (.D(i22), .en(we), .Q(o22), .clk(clk), .clr(rst));
  Register #(.width(32)) _26 (.D(i26), .en(we), .Q(o26), .clk(clk), .clr(rst));
  Register #(.width(32)) _30 (.D(i30), .en(we), .Q(o30), .clk(clk), .clr(rst));
  Register #(.width(32)) _3 (.D(i3), .en(we), .Q(o3), .clk(clk), .clr(rst));
  Register #(.width(32)) _7 (.D(i7), .en(we), .Q(o7), .clk(clk), .clr(rst));
  Register #(.width(32)) _11 (.D(i11), .en(we), .Q(o11), .clk(clk), .clr(rst));
  Register #(.width(32)) _15 (.D(i15), .en(we), .Q(o15), .clk(clk), .clr(rst));
  Register #(.width(32)) _19 (.D(i19), .en(we), .Q(o19), .clk(clk), .clr(rst));
  Register #(.width(32)) _23 (.D(i23), .en(we), .Q(o23), .clk(clk), .clr(rst));
  Register #(.width(32)) _27 (.D(i27), .en(we), .Q(o27), .clk(clk), .clr(rst));
  Register #(.width(32)) _31 (.D(i31), .en(we), .Q(o31), .clk(clk), .clr(rst));
  Multiplexer #(.select(5), .width(32)) multiplexer_1 (
    .in0(o0), .in1(o1), .in2(o2), .in3(o3), .in4(o4), .in5(o5), .in6(o6), .in7(o7), .in8(o8), .in9(o9),
    .in10(o10), .in11(o11), .in12(o12), .in13(o13), .in14(o14), .in15(o15), .in16(o16), .in17(o17),
    .in18(o18), .in19(o19), .in20(o20), .in21(o21), .in22(o22), .in23(o23), .in24(o24), .in25(o25),
    .in26(o26), .in27(o27), .in28(o28), .in29(o29), .in30(o30), .in31(o31), .out(RD1), .sel(A1));  // open: en
  Multiplexer #(.select(5), .width(32)) multiplexer_2 (
    .in0(o0), .in1(o1), .in2(o2), .in3(o3), .in4(o4), .in5(o5), .in6(o6), .in7(o7), .in8(o8), .in9(o9),
    .in10(o10), .in11(o11), .in12(o12), .in13(o13), .in14(o14), .in15(o15), .in16(o16), .in17(o17),
    .in18(o18), .in19(o19), .in20(o20), .in21(o21), .in22(o22), .in23(o23), .in24(o24), .in25(o25),
    .in26(o26), .in27(o27), .in28(o28), .in29(o29), .in30(o30), .in31(o31), .out(RD2), .sel(A2));  // open: en
endmodule

module main (
  input  in_1,
  output [31:0] out_2,
  output [31:0] out_3,
  output out_4,
  output [4:0] out_5,
  output [31:0] out_6,
  output out_7,
  output [31:0] out_8,
  output [31:0] out_9
);

  wire Br, BSel, clk, EXTOp, zero;
  wire [1:0] jal_jr, WDSel, WRSel;
  wire [2:0] ALUOp;
  wire [31:0] dm_1_rd, ext_1_out_3, multiplexer_3_out, npc_1_npc, npc_1_pc_4, pc, rf_1_rd1;

  Register #(.width(32)) u_PC (.D(npc_1_npc), .Q(pc), .clk(clk), .clr(in_1));  // open: en
  NPC npc_1 (
    .NPC(npc_1_npc), .PC(pc), .Imm(ext_1_out_3), .zero(Br), .PC_4(npc_1_pc_4), .in_2(out_2[25:0]), .Br(zero),
    .jal(jal_jr), .in_4(out_8));
  Clock clock_1 (.out(clk));
  Controller controller_1 (
    .op(out_2[31:26]), .func(out_2[5:0]), .EXTOp(EXTOp), .Bsel(BSel), .ALUOp(ALUOp), .Br(Br), .DMWr(out_7),
    .WDSel(WDSel), .WRSel(WRSel), .RFWr(out_4), .jal(jal_jr));
  ROM #(.addrWidth(12), .dataWidth(32)) rom_1 (.addr(pc[13:2]), .data(out_2));  // open: sel
  EXT ext_1 (.in_2(out_2[15:0]), .EXTOp(EXTOp), .out_3(ext_1_out_3));
  Multiplexer #(.select(2), .width(5)) multiplexer_1 (
    .in0(out_2[20:16]), .in1(out_2[15:11]), .in2({5{1'b1}}), .out(out_5), .sel(WRSel));  // open: in3, en
  Multiplexer #(.select(2), .width(32)) multiplexer_2 (
    .in0(out_8), .in1(dm_1_rd), .in2(npc_1_pc_4), .out(out_6), .sel(WDSel));  // open: in3, en
  Adder #(.width(32)) adder_1 (.a(pc), .b(32'h3000), .out(out_3));  // open: cin, cout
  RF rf_1 (
    .A1(out_2[25:21]), .A2(out_2[20:16]), .A3(out_5), .WD(out_6), .RD1(rf_1_rd1), .RD2(out_9), .clk(clk),
    .rst(in_1), .we(out_4));
  Multiplexer #(.width(32)) multiplexer_3 (
    .in0(out_9), .in1(ext_1_out_3), .out(multiplexer_3_out), .sel(BSel));  // open: en
  ALU alu_1 (.A(rf_1_rd1), .B(multiplexer_3_out), .zero(zero), .C(out_8), .Sel(ALUOp));
  DM dm_1 (.Addr(out_8), .WD(out_9), .RD(dm_1_rd), .DMWr(out_7), .clk(clk), .rst(in_1));

  // Other names for the same wires on the sheet: DMWr = out_7; func[5:0] = out_2[5:0]; Instr[31:0] = out_2;
  //   shamt[4:0] = out_2[10:6]; op[5:0] = out_2[31:26]; memAddr[31:0] = out_8; memData[31:0] = out_9;
  //   regAddr[4:0] = out_5; regData[31:0] = out_6; RFWr = out_4; rst = in_1

  // Notes on the sheet:
  //   contents of rom_1 (hex, n*v repeats v):
  //   341c0000 341d0000 34013456 210820 8c010004 ac010004 3c027878 411822 3c051234 34040005 0 ac85ffff
  //   8c83ffff 10650003 0 10000011 0 34670404 10e3000e 0 3c087777 3508ffff 80022 34001100 e65020 34080000
  //   34090001 340a0001 10a4020 1109fffe c000c22 0 14a5020 1000ffff 14a5020 3e00008
endmodule

module ALU (
  input  [2:0] Sel,
  input  [31:0] A,
  input  [31:0] B,
  output zero,
  output [31:0] C
);

  wire [31:0] adder_1_out, adder_2_out, adder_3_out, not_1_out, or_1_out;

  assign not_1_out = ~B;  // NOT_Gate not_1, 32 bits wide
  assign or_1_out = B | A;  // OR_Gate or_1, 32 bits wide
  Adder #(.width(32)) adder_1 (.a(not_1_out), .b(32'h1), .out(adder_1_out));  // open: cin, cout
  Adder #(.width(32)) adder_2 (.a(A), .b(B), .out(adder_2_out));  // open: cin, cout
  Adder #(.width(32)) adder_3 (.a(A), .b(adder_1_out), .out(adder_3_out));  // open: cin, cout
  Multiplexer #(.select(3), .width(32)) multiplexer_1 (
    .in0(adder_2_out), .in1(adder_3_out), .in2(or_1_out), .in3({B[15:0], {16{1'b0}}}), .in4(A), .out(C),
    .sel(Sel));  // open: in5, in6, in7, en
  zero zero_1 (.in_1(C), .out_2(zero));

  // Other names for the same wires on the sheet: slt[2:0] = Sel
endmodule

module zero (
  input  [31:0] in_1,
  output out_2
);

  wire or_1_out, or_2_out, or_3_out, or_4_out, or_5_out, or_6_out, or_7_out, or_8_out;

  or or_1 (or_1_out, in_1[0], in_1[1], in_1[2], in_1[3], in_1[4]);
  or or_2 (or_2_out, in_1[5], in_1[6], in_1[7], in_1[8], in_1[9]);
  or or_3 (or_3_out, in_1[10], in_1[11], in_1[12], in_1[13], in_1[14]);
  or or_4 (or_4_out, in_1[15], in_1[16], in_1[17], in_1[18], in_1[19]);
  or or_5 (or_5_out, in_1[20], in_1[21], in_1[22], in_1[23], in_1[24]);
  or or_6 (or_6_out, in_1[25], in_1[26], in_1[27], in_1[28], in_1[29]);
  or or_7 (or_7_out, in_1[30], in_1[31]);
  not not_1 (out_2, or_8_out);
  or or_8 (or_8_out, or_1_out, or_2_out, or_3_out, or_4_out, or_5_out, or_6_out, or_7_out);
endmodule

module EXT (
  input  EXTOp,
  input  [15:0] in_2,
  output [31:0] out_3
);

  wire [31:0] bit_extender_1_out, bit_extender_2_out;

  assign bit_extender_1_out = {{16{1'b0}}, in_2};  // Bit_Extender bit_extender_1
  assign bit_extender_2_out = {{16{in_2[15]}}, in_2};  // Bit_Extender bit_extender_2
  Multiplexer #(.width(32)) multiplexer_1 (
    .in0(bit_extender_1_out), .in1(bit_extender_2_out), .out(out_3), .sel(EXTOp));  // open: en

  // Other names for the same wires on the sheet: slt = EXTOp
endmodule

module NPC (
  input  [31:0] PC,
  input  [25:0] in_2,
  input  [31:0] Imm,
  input  [31:0] in_4,
  input  [1:0] jal,
  input  Br,
  input  zero,
  output [31:0] NPC,
  output [31:0] PC_4
);

  wire and_1_out;
  wire [31:0] adder_2_out, multiplexer_1_out, shifter_1_out;

  Adder #(.width(32)) adder_1 (.a(32'h4), .b(PC), .out(PC_4));  // open: cin, cout
  Shifter #(.width(32)) shifter_1 (.in(Imm), .\dist (5'b00010), .out(shifter_1_out));
  Adder #(.width(32)) adder_2 (.a(PC_4), .b(shifter_1_out), .out(adder_2_out));  // open: cin, cout
  Multiplexer #(.width(32)) multiplexer_1 (
    .in0(PC_4), .in1(adder_2_out), .out(multiplexer_1_out), .sel(and_1_out));  // open: en
  and and_1 (and_1_out, Br, zero);
  Multiplexer #(.select(2), .width(32)) multiplexer_2 (
    .in0(multiplexer_1_out), .in1({PC[31:28], in_2, 2'b00}), .in2(in_4), .out(NPC), .sel(jal));  // open: in3, en

  // Other names for the same wires on the sheet: Imm_26[25:0] = in_2; ra[31:0] = in_4
endmodule

module Controller (
  input  [5:0] op,
  input  [5:0] func,
  output EXTOp,
  output Bsel,
  output [2:0] ALUOp,
  output Br,
  output DMWr,
  output [1:0] WDSel,
  output [1:0] WRSel,
  output RFWr,
  output [1:0] jal
);

  wire andctrl_1_add, andctrl_1_beq, andctrl_1_jal, andctrl_1_jr, andctrl_1_lui, andctrl_1_lw, andctrl_1_ori,
       andctrl_1_sub, andctrl_1_sw;

  andCtrl andctrl_1 (
    .op(op), .func(func), .add(andctrl_1_add), .sub(andctrl_1_sub), .ori(andctrl_1_ori), .lw(andctrl_1_lw),
    .sw(andctrl_1_sw), .beq(andctrl_1_beq), .lui(andctrl_1_lui), .jal(andctrl_1_jal), .jr(andctrl_1_jr));
  orCtrl orctrl_1 (
    .add(andctrl_1_add), .sub(andctrl_1_sub), .ori(andctrl_1_ori), .lw(andctrl_1_lw), .sw(andctrl_1_sw),
    .beq(andctrl_1_beq), .lui(andctrl_1_lui), .jal(andctrl_1_jal), .jr(andctrl_1_jr), .EXTOp(EXTOp),
    .Bsel(Bsel), .ALUOp(ALUOp), .Br(Br), .DMWr(DMWr), .WDSel(WDSel), .WRSel(WRSel), .RFWr(RFWr), .jal_jr(jal));
endmodule

// and
module andCtrl (
  input  [5:0] op,
  input  [5:0] func,
  output add,
  output sub,
  output ori,
  output lw,
  output sw,
  output beq,
  output lui,
  output jal,
  output jr
);

  wire and_1_out, and_2_out, and_3_out, and_4_out, and_11_out, and_12_out, not_1_out, not_2_out, not_3_out,
       not_4_out, not_5_out, not_6_out, not_7_out, not_8_out, not_9_out, not_10_out, not_11_out, not_12_out;

  not not_1 (not_1_out, op[5]);
  not not_2 (not_2_out, op[3]);
  not not_3 (not_3_out, op[4]);
  not not_4 (not_4_out, op[1]);
  not not_5 (not_5_out, op[2]);
  not not_6 (not_6_out, op[0]);
  not not_7 (not_7_out, func[5]);
  not not_8 (not_8_out, func[4]);
  not not_9 (not_9_out, func[3]);
  not not_10 (not_10_out, func[1]);
  not not_11 (not_11_out, func[2]);
  not not_12 (not_12_out, func[0]);
  and and_1 (and_1_out, not_1_out, not_3_out, not_2_out, not_5_out, not_4_out, not_6_out);
  and and_2 (and_2_out, func[5], not_8_out, not_9_out, not_11_out, not_10_out, not_12_out);
  and and_3 (and_3_out, not_1_out, not_3_out, not_2_out, not_5_out, not_4_out, not_6_out);
  and and_4 (and_4_out, func[5], not_8_out, not_9_out, not_11_out, func[1], not_12_out);
  and and_5 (ori, not_1_out, not_3_out, op[3], op[2], not_4_out, op[0]);
  and and_6 (lw, op[5], not_3_out, not_2_out, not_5_out, op[1], op[0]);
  and and_7 (sw, op[5], not_3_out, op[3], not_5_out, op[1], op[0]);
  and and_8 (beq, not_1_out, not_3_out, not_2_out, op[2], not_4_out, not_6_out);
  and and_9 (lui, not_1_out, not_3_out, op[3], op[2], op[1], op[0]);
  and and_10 (jal, not_1_out, not_3_out, not_2_out, not_5_out, op[1], op[0]);
  and and_11 (and_11_out, not_1_out, not_3_out, not_2_out, not_5_out, not_4_out, not_6_out);
  and and_12 (and_12_out, not_7_out, not_8_out, func[3], not_11_out, not_10_out, not_12_out);
  and and_13 (add, and_1_out, and_2_out);
  and and_14 (sub, and_3_out, and_4_out);
  and and_15 (jr, and_11_out, and_12_out);
endmodule

// or
module orCtrl (
  input  add,
  input  sub,
  input  ori,
  input  lw,
  input  sw,
  input  beq,
  input  lui,
  input  jal,
  input  jr,
  output Br,
  output DMWr,
  output RFWr,
  output EXTOp,
  output Bsel,
  output [2:0] ALUOp,
  output [1:0] WDSel,
  output [1:0] WRSel,
  output [1:0] jal_jr
);

  or or_1 (EXTOp, beq, lui, sw, lw);
  buf or_2 (ALUOp[2], jr);  // OR_Gate
  or or_3 (Bsel, sw, lui, lw, ori);
  or or_4 (ALUOp[1], ori, lui);
  or or_5 (ALUOp[0], sub, beq, lui);
  buf or_6 (Br, beq);  // OR_Gate
  buf or_7 (DMWr, sw);  // OR_Gate
  buf or_8 (WDSel[0], lw);  // OR_Gate
  buf or_9 (WDSel[1], jal);  // OR_Gate
  buf or_10 (WRSel[1], jal);  // OR_Gate
  or or_11 (WRSel[0], add, sub);
  or or_12 (RFWr, lui, add, sub, ori, lw, jal);
  buf or_13 (jal_jr[0], jal);  // OR_Gate
  buf or_14 (jal_jr[1], jr);  // OR_Gate
endmodule

module DM (
  input  [31:0] Addr,
  input  DMWr,
  input  clk,
  input  rst,
  input  [31:0] WD,
  output [31:0] RD
);

  RAM #(.addrWidth(12), .dataWidth(32), .bus("separate")) ram_1 (
    .addr(Addr[13:2]), .din(WD), .data(RD), .str(DMWr), .clk(clk), .clr(rst));  // open: sel, ld
endmodule
