// Logisim project 4bit_sort.circ as structural Verilog: 3 circuits, main circuit 4bit_sort
module _4bit_sort (
  input  [3:0] A,
  input  [3:0] B,
  input  [3:0] C,
  input  [3:0] D,
  output [3:0] _1,
  output [3:0] _2,
  output [3:0] _3,
  output [3:0] _4
);

  wire comparator_1_gt, comparator_2_gt, comparator_3_gt, comparator_4_gt, comparator_5_gt, comparator_6_gt;
  wire [3:0] n4bit_swap_1_out_4, n4bit_swap_1_out_5, n4bit_swap_2_out_4, n4bit_swap_2_out_5,
       n4bit_swap_3_out_4, n4bit_swap_3_out_5, n4bit_swap_4_out_4, n4bit_swap_5_out_4;

  Comparator #(.width(4), .mode("unsigned")) comparator_1 (.a(A), .b(B), .gt(comparator_1_gt));  // open: eq, lt
  _4bit_swap u_4bit_swap_1 (
    .in1(A), .in2(B), .in_3(comparator_1_gt), .out_4(n4bit_swap_1_out_4), .out_5(n4bit_swap_1_out_5));
  Comparator #(.width(4), .mode("unsigned")) comparator_2 (
    .a(n4bit_swap_1_out_5), .b(C), .gt(comparator_2_gt));  // open: eq, lt
  _4bit_swap u_4bit_swap_2 (
    .in1(n4bit_swap_1_out_5), .in2(C), .in_3(comparator_2_gt), .out_4(n4bit_swap_2_out_4),
    .out_5(n4bit_swap_2_out_5));
  Comparator #(.width(4), .mode("unsigned")) comparator_3 (
    .a(n4bit_swap_1_out_4), .b(n4bit_swap_2_out_4), .gt(comparator_3_gt));  // open: eq, lt
  Comparator #(.width(4), .mode("unsigned")) comparator_4 (
    .a(n4bit_swap_2_out_5), .b(D), .gt(comparator_4_gt));  // open: eq, lt
  _4bit_swap u_4bit_swap_3 (
    .in1(n4bit_swap_1_out_4), .in2(n4bit_swap_2_out_4), .in_3(comparator_3_gt), .out_4(n4bit_swap_3_out_4),
    .out_5(n4bit_swap_3_out_5));
  _4bit_swap u_4bit_swap_4 (
    .in1(n4bit_swap_2_out_5), .in2(D), .in_3(comparator_4_gt), .out_4(n4bit_swap_4_out_4), .out_5(_4));
  Comparator #(.width(4), .mode("unsigned")) comparator_5 (
    .a(n4bit_swap_3_out_5), .b(n4bit_swap_4_out_4), .gt(comparator_5_gt));  // open: eq, lt
  _4bit_swap u_4bit_swap_5 (
    .in1(n4bit_swap_3_out_5), .in2(n4bit_swap_4_out_4), .in_3(comparator_5_gt), .out_4(n4bit_swap_5_out_4),
    .out_5(_3));
  Comparator #(.width(4), .mode("unsigned")) comparator_6 (
    .a(n4bit_swap_3_out_4), .b(n4bit_swap_5_out_4), .gt(comparator_6_gt));  // open: eq, lt
  _4bit_swap u_4bit_swap_6 (
    .in1(n4bit_swap_3_out_4), .in2(n4bit_swap_5_out_4), .in_3(comparator_6_gt), .out_4(_1), .out_5(_2));
endmodule

module _1bit_swap (
  input  I1,
  input  I2,
  input  S,
  output O1,
  output O2
);

  wire I1_nS_out, I1_S_out, I2_nS_out, I2_S_out, not_1_out;

  not not_1 (not_1_out, S);
  and I1_S (I1_S_out, I1, S);
  and I2_S (I2_S_out, I2, S);
  and I1_nS (I1_nS_out, I1, not_1_out);
  and I2_nS (I2_nS_out, I2, not_1_out);
  or or_1 (O1, I2_S_out, I1_nS_out);
  or or_2 (O2, I1_S_out, I2_nS_out);
endmodule

module _4bit_swap (
  input  [3:0] in1,
  input  [3:0] in2,
  input  in_3,
  output [3:0] out_4,
  output [3:0] out_5
);

  _1bit_swap u_1bit_swap_1 (.I1(in1[0]), .I2(in2[0]), .S(in_3), .O1(out_4[0]), .O2(out_5[0]));
  _1bit_swap u_1bit_swap_2 (.I1(in1[1]), .I2(in2[1]), .S(in_3), .O1(out_4[1]), .O2(out_5[1]));
  _1bit_swap u_1bit_swap_3 (.I1(in1[2]), .I2(in2[2]), .S(in_3), .O1(out_4[2]), .O2(out_5[2]));
  _1bit_swap u_1bit_swap_4 (.I1(in1[3]), .I2(in2[3]), .S(in_3), .O1(out_4[3]), .O2(out_5[3]));
endmodule
