// Logisim project Adder.circ as structural Verilog
// 1_bit
module adder_1bit (
  input  A,
  input  B,
  input  CI,
  output CO,
  output SO
);

  wire nand_1_out, nand_2_out, xor_1_out;

  xor xor_1 (xor_1_out, A, B);
  nand nand_1 (nand_1_out, A, B);
  nand nand_2 (nand_2_out, CI, xor_1_out);
  nand nand_3 (CO, nand_1_out, nand_2_out);
  xor xor_2 (SO, xor_1_out, CI);
endmodule

module adder_4bit (
  input  [3:0] A,
  input  [3:0] B,
  input  CI0,
  output CO3,
  output [3:0] S
);

  wire adder_1bit_2_co, adder_1bit_3_co, adder_1bit_4_co;

  adder_1bit adder_1bit_1 (.A(A[3]), .B(B[3]), .CI(adder_1bit_2_co), .CO(CO3), .SO(S[3]));
  adder_1bit adder_1bit_2 (.A(A[2]), .B(B[2]), .CI(adder_1bit_3_co), .CO(adder_1bit_2_co), .SO(S[2]));
  adder_1bit adder_1bit_3 (.A(A[1]), .B(B[1]), .CI(adder_1bit_4_co), .CO(adder_1bit_3_co), .SO(S[1]));
  adder_1bit adder_1bit_4 (.A(A[0]), .B(B[0]), .CI(CI0), .CO(adder_1bit_4_co), .SO(S[0]));
endmodule

module adder_4bit_improve (
  input  [3:0] A,
  input  [3:0] B,
  input  C0,
  output C4,
  output [3:0] S
);

  wire _01_out, _012_out, _12_out, _23_out, _123_out, _0124_out, C01_out, C1_out, C2_out, C3_out, C012_out,
       C0124_out, CP0_out, G0_out, G0P1_out, G0P12_out, G0P123_out, G1_out, G1P2_out, G1P23_out, G2_out,
       G2P3_out, G3_out, P0_out, P1_out, P2_out, P3_out;

  and G3 (G3_out, A[3], B[3]);
  xor P3 (P3_out, A[3], B[3]);
  and G2 (G2_out, A[2], B[2]);
  xor P2 (P2_out, A[2], B[2]);
  and G1 (G1_out, A[1], B[1]);
  xor P1 (P1_out, A[1], B[1]);
  and G0 (G0_out, A[0], B[0]);
  xor P0 (P0_out, A[0], B[0]);
  and CP0 (CP0_out, C0, P0_out);
  and _23 (_23_out, P3_out, P2_out);
  and _12 (_12_out, P2_out, P1_out);
  and _01 (_01_out, P1_out, P0_out);
  and G2P3 (G2P3_out, P3_out, G2_out);
  and G1P2 (G1P2_out, P2_out, G1_out);
  and C01 (C01_out, _01_out, C0);
  and G1P23 (G1P23_out, G1_out, _23_out);
  and _123 (_123_out, _23_out, _12_out);
  and G0P12 (G0P12_out, G0_out, _12_out);
  and _012 (_012_out, _12_out, _01_out);
  and G0P123 (G0P123_out, _123_out, G0_out);
  and C012 (C012_out, _012_out, C0);
  and G0P1 (G0P1_out, P1_out, G0_out);
  and _0124 (_0124_out, _123_out, _012_out);
  and C0124 (C0124_out, _0124_out, C0);
  or u_C4 (C4, G3_out, G2P3_out, G1P23_out, G0P123_out, C0124_out);
  or C3 (C3_out, C012_out, G2_out, G1P2_out, G0P12_out);
  or C2 (C2_out, G1_out, G0P1_out, C01_out);
  or C1 (C1_out, G0_out, CP0_out);
  xor xor_1 (S[3], P3_out, C3_out);
  xor xor_2 (S[2], P2_out, C2_out);
  xor xor_3 (S[1], C1_out, P1_out);
  xor xor_4 (S[0], P0_out, C0);
endmodule
