// Logisim project CRC.circ as structural Verilog: 2 circuits, main circuit CRC
module CRC (
  input  [7:0] in_1,
  input  [3:0] in_2,
  output [10:0] out_3
);

  wire [2:0] \moddiv_4bit_1_余数 , \moddiv_4bit_2_余数 , \moddiv_4bit_3_余数 , \moddiv_4bit_4_余数 ,
       \moddiv_4bit_5_余数 , \moddiv_4bit_6_余数 , \moddiv_4bit_7_余数 ;

  moddiv_4bit moddiv_4bit_1 (.\被除数 (in_1[7:4]), .\除数 (in_2), .\余数 (\moddiv_4bit_1_余数 ));  // open: 商
  moddiv_4bit moddiv_4bit_2 (.\被除数 ({\moddiv_4bit_1_余数 , in_1[3]}), .\除数 (in_2), .\余数 (\moddiv_4bit_2_余数 ));  // open: 商
  moddiv_4bit moddiv_4bit_3 (.\被除数 ({\moddiv_4bit_2_余数 , in_1[2]}), .\除数 (in_2), .\余数 (\moddiv_4bit_3_余数 ));  // open: 商
  moddiv_4bit moddiv_4bit_4 (.\被除数 ({\moddiv_4bit_3_余数 , in_1[1]}), .\除数 (in_2), .\余数 (\moddiv_4bit_4_余数 ));  // open: 商
  moddiv_4bit moddiv_4bit_5 (.\被除数 ({\moddiv_4bit_4_余数 , in_1[0]}), .\除数 (in_2), .\余数 (\moddiv_4bit_5_余数 ));  // open: 商
  moddiv_4bit moddiv_4bit_6 (.\被除数 ({\moddiv_4bit_5_余数 , 1'b0}), .\除数 (in_2), .\余数 (\moddiv_4bit_6_余数 ));  // open: 商
  moddiv_4bit moddiv_4bit_7 (.\被除数 ({\moddiv_4bit_6_余数 , 1'b0}), .\除数 (in_2), .\余数 (\moddiv_4bit_7_余数 ));  // open: 商
  moddiv_4bit moddiv_4bit_8 (.\被除数 ({\moddiv_4bit_7_余数 , 1'b0}), .\除数 (in_2), .\余数 (out_3[2:0]));  // open: 商

  assign out_3[10:3] = in_1;

  // Other names for the same wires on the sheet: div[3:0] = in_2; input[7:0] = in_1
endmodule

module moddiv_4bit (
  input  [3:0] \被除数 ,
  input  [3:0] \除数 ,
  output [2:0] \余数 ,
  output \商 
);

  wire [3:0] xor_1_out;
  wire [3:3] multiplexer_1_out;

  assign xor_1_out = \被除数  ^ \除数 ;  // XOR_Gate xor_1, 4 bits wide
  Multiplexer #(.width(4)) multiplexer_1 (
    .in0(\被除数 ), .in1(xor_1_out), .out({multiplexer_1_out[3], \余数 }), .sel(\被除数 [3]));  // open: en

  assign \商  = \被除数 [3];

  // Other names for the same wires on the sheet: slt = \被除数 [3]
endmodule
