// Logisim project Fibonacci.circ as structural Verilog: 3 circuits, main circuit main
module main (
  input  [2:0] in_1,
  input  in_2,
  output [3:0] out_3
);

  wire stop;
  wire [3:0] f_now;

  // Probe on stop
  count count_1 (.in_1(in_1), .reset(in_2), .out_3(stop));
  calculate calculate_1 (.stop(stop), .in_2(in_2), .out_3(f_now));
  // Probe on f_now
  Multiplexer #(.width(4)) multiplexer_1 (.in0(4'b0000), .in1(f_now), .out(out_3), .sel(stop));  // open: en

  // Other names for the same wires on the sheet: reset = in_2
endmodule

module calculate (
  input  stop,
  input  in_2,
  output [3:0] out_3
);

  wire clock, enable, \initial ;
  wire [3:0] adder_1_out, multiplexer_1_out, prev;

  Clock clock_1 (.out(clock));
  Counter #(.width(1), .max('h1), .ongoal("stay")) counter_1 (
    .Q(\initial ), .clk(clock), .clr(in_2));  // open: load, D, count, carry
  not not_1 (enable, stop);
  Multiplexer #(.width(4)) multiplexer_1 (
    .in0(4'b0001), .in1(out_3), .out(multiplexer_1_out), .sel(\initial ));  // open: en
  Adder #(.width(4)) adder_1 (.a(prev), .b(out_3), .out(adder_1_out));  // open: cin, cout
  Register #(.width(4)) u_prev (.D(multiplexer_1_out), .en(enable), .Q(prev), .clk(clock), .clr(in_2));
  Register #(.width(4)) now (.D(adder_1_out), .en(enable), .Q(out_3), .clk(clock), .clr(in_2));

  // Other names for the same wires on the sheet: now[3:0] = out_3; reset = in_2
endmodule

module count (
  input  [2:0] in_1,
  input  reset,
  output out_3
);

  wire clock_1_out;
  wire [3:0] bit_extender_1_out, counter_1_q;

  Clock clock_1 (.out(clock_1_out));
  assign bit_extender_1_out = {{1{1'b0}}, in_1};  // Bit_Extender bit_extender_1
  Counter #(.width(4), .max('hf), .ongoal("stay")) counter_1 (
    .Q(counter_1_q), .clk(clock_1_out), .clr(reset));  // open: load, D, count, carry
  Comparator #(.width(4), .mode("unsigned")) comparator_1 (
    .a(bit_extender_1_out), .b(counter_1_q), .lt(out_3));  // open: gt, eq
endmodule
