// Logisim project Fibonacci_improve.circ as structural Verilog: 8 circuits, main circuit main
module main (
  input  [31:0] \input ,
  output [31:0] \output 
);

  wire freeze, now;

  \计数逻辑  \u_计数逻辑  (.\input (\input ), .in_2(1'b0), .now(now), .freeze(freeze));
  \计算逻辑  \u_计算逻辑  (.in_1(now), .in_2(freeze), .in_3(1'b0), .out_4(\output ));
endmodule

module \寄存器矩阵  (
  input  [31:0] in_11,
  input  [31:0] in_12,
  input  [31:0] in_21,
  input  [31:0] in_22,
  input  ena,
  input  clk,
  input  clr,
  output [31:0] out_11,
  output [31:0] out_12,
  output [31:0] out_21,
  output [31:0] out_22
);

  Register #(.width(32)) register_1 (.D(in_11), .en(ena), .Q(out_11), .clk(clk), .clr(clr));
  Register #(.width(32)) register_2 (.D(in_12), .en(ena), .Q(out_12), .clk(clk), .clr(clr));
  Register #(.width(32)) register_3 (.D(in_21), .en(ena), .Q(out_21), .clk(clk), .clr(clr));
  Register #(.width(32)) register_4 (.D(in_22), .en(ena), .Q(out_22), .clk(clk), .clr(clr));
endmodule

module \矩阵乘法  (
  input  [31:0] in1_11,
  input  [31:0] in1_12,
  input  [31:0] in1_21,
  input  [31:0] in1_22,
  input  [31:0] in2_11,
  input  [31:0] in2_12,
  input  [31:0] in2_21,
  input  [31:0] in2_22,
  output [31:0] out_11,
  output [31:0] out_12,
  output [31:0] out_21,
  output [31:0] out_22
);

  wire [31:0] multiplier_1_out, multiplier_2_out, multiplier_3_out, multiplier_4_out, multiplier_5_out,
       multiplier_6_out, multiplier_7_out, multiplier_8_out;

  Multiplier #(.width(32)) multiplier_1 (.a(in1_11), .b(in2_11), .out(multiplier_1_out));  // open: cin, cout
  Multiplier #(.width(32)) multiplier_2 (.a(in1_12), .b(in2_21), .out(multiplier_2_out));  // open: cin, cout
  Multiplier #(.width(32)) multiplier_3 (.a(in1_11), .b(in2_12), .out(multiplier_3_out));  // open: cin, cout
  Multiplier #(.width(32)) multiplier_4 (.a(in1_12), .b(in2_22), .out(multiplier_4_out));  // open: cin, cout
  Multiplier #(.width(32)) multiplier_5 (.a(in1_21), .b(in2_11), .out(multiplier_5_out));  // open: cin, cout
  Multiplier #(.width(32)) multiplier_6 (.a(in1_22), .b(in2_21), .out(multiplier_6_out));  // open: cin, cout
  Multiplier #(.width(32)) multiplier_7 (.a(in1_21), .b(in2_12), .out(multiplier_7_out));  // open: cin, cout
  Multiplier #(.width(32)) multiplier_8 (.a(in1_22), .b(in2_22), .out(multiplier_8_out));  // open: cin, cout
  Adder #(.width(32)) adder_1 (.a(multiplier_1_out), .b(multiplier_2_out), .out(out_11));  // open: cin, cout
  Adder #(.width(32)) adder_2 (.a(multiplier_3_out), .b(multiplier_4_out), .out(out_12));  // open: cin, cout
  Adder #(.width(32)) adder_3 (.a(multiplier_5_out), .b(multiplier_6_out), .out(out_21));  // open: cin, cout
  Adder #(.width(32)) adder_4 (.a(multiplier_7_out), .b(multiplier_8_out), .out(out_22));  // open: cin, cout

  // Other names for the same wires on the sheet: _1_11[31:0] = in1_11; _1_12[31:0] = in1_12; _1_21[31:0] = in1_21;
  //   _1_22[31:0] = in1_22; _2_11[31:0] = in2_11; _2_12[31:0] = in2_12; _2_21[31:0] = in2_21; _2_22[31:0] = in2_22
endmodule

module \矩阵选择  (
  input  [31:0] in1_11,
  input  [31:0] in1_12,
  input  [31:0] in1_21,
  input  [31:0] in1_22,
  input  [31:0] in2_11,
  input  [31:0] in2_12,
  input  [31:0] in2_21,
  input  [31:0] in2_22,
  input  in_9,
  output [31:0] out_11,
  output [31:0] out_12,
  output [31:0] out_21,
  output [31:0] out_22
);

  Multiplexer #(.width(32)) multiplexer_1 (.in0(in1_11), .in1(in2_11), .out(out_11), .sel(in_9));  // open: en
  Multiplexer #(.width(32)) multiplexer_2 (.in0(in1_12), .in1(in2_12), .out(out_12), .sel(in_9));  // open: en
  Multiplexer #(.width(32)) multiplexer_3 (.in0(in1_21), .in1(in2_21), .out(out_21), .sel(in_9));  // open: en
  Multiplexer #(.width(32)) multiplexer_4 (.in0(in1_22), .in1(in2_22), .out(out_22), .sel(in_9));  // open: en

  // Other names for the same wires on the sheet: _1_11[31:0] = in1_11; _1_12[31:0] = in1_12; _1_21[31:0] = in1_21;
  //   _1_22[31:0] = in1_22; _2_11[31:0] = in2_11; _2_12[31:0] = in2_12; _2_21[31:0] = in2_21; _2_22[31:0] = in2_22;
  //   slt = in_9
endmodule

module \初始矩阵  (
  output [31:0] out_11,
  output [31:0] out_12,
  output [31:0] out_21,
  output [31:0] out_22
);


  assign out_11 = 32'h1;
  assign out_12 = 32'h1;
  assign out_21 = 32'h1;
  assign out_22 = {32{1'b0}};
endmodule

module \单位矩阵  (
  output [31:0] out_11,
  output [31:0] out_12,
  output [31:0] out_21,
  output [31:0] out_22
);


  assign out_11 = 32'h1;
  assign out_12 = {32{1'b0}};
  assign out_21 = {32{1'b0}};
  assign out_22 = 32'h1;
endmodule

module \计算逻辑  (
  input  in_1,
  input  in_2,
  input  in_3,
  output [31:0] out_4
);

  wire clk, ena, init;
  wire [31:0] a11, a12, a21, a22, A_2_out_11, A_2_out_12, A_2_out_21, A_2_out_22, MUX_2_out_11, MUX_2_out_12,
       MUX_2_out_21, MUX_2_out_22, MUX_3_out_11, MUX_3_out_12, MUX_3_out_21, MUX_3_out_22, MUX_out_11,
       MUX_out_12, MUX_out_21, MUX_out_22, s11, s12, s21, s22, S_A_out_11, S_A_out_12, S_A_out_21,
       S_A_out_22, \初始值_out_11 , \初始值_out_12 , \初始值_out_21 , \初始值_out_22 , \单位阵_2_out_11 , \单位阵_2_out_12 ,
       \单位阵_2_out_21 , \单位阵_2_out_22 , \单位阵_out_11 , \单位阵_out_12 , \单位阵_out_21 , \单位阵_out_22 ;

  Counter #(.width(1), .max('h1), .ongoal("stay")) counter_1 (
    .Q(init), .clk(clk), .clr(in_3));  // open: load, D, count, carry
  Clock clock_1 (.out(clk));
  not not_1 (ena, in_2);
  \单位矩阵  \u_单位阵  (.out_11(\单位阵_out_11 ), .out_12(\单位阵_out_12 ), .out_21(\单位阵_out_21 ), .out_22(\单位阵_out_22 ));
  \矩阵选择  MUX (
    .in1_11(\单位阵_out_11 ), .in1_12(\单位阵_out_12 ), .in1_21(\单位阵_out_21 ), .in1_22(\单位阵_out_22 ), .in2_11(a11),
    .in2_12(a12), .in2_21(a21), .in2_22(a22), .in_9(in_1), .out_11(MUX_out_11), .out_12(MUX_out_12),
    .out_21(MUX_out_21), .out_22(MUX_out_22));
  \矩阵乘法  A_2 (
    .in1_11(a11), .in1_12(a12), .in1_21(a21), .in1_22(a22), .in2_11(a11), .in2_12(a12), .in2_21(a21),
    .in2_22(a22), .out_11(A_2_out_11), .out_12(A_2_out_12), .out_21(A_2_out_21), .out_22(A_2_out_22));
  \矩阵乘法  S_A (
    .in1_11(s11), .in1_12(s12), .in1_21(s21), .in1_22(s22), .in2_11(MUX_out_11), .in2_12(MUX_out_12),
    .in2_21(MUX_out_21), .in2_22(MUX_out_22), .out_11(S_A_out_11), .out_12(S_A_out_12), .out_21(S_A_out_21),
    .out_22(S_A_out_22));
  \初始矩阵  \u_初始值  (.out_11(\初始值_out_11 ), .out_12(\初始值_out_12 ), .out_21(\初始值_out_21 ), .out_22(\初始值_out_22 ));
  \矩阵选择  MUX_2 (
    .in1_11(\初始值_out_11 ), .in1_12(\初始值_out_12 ), .in1_21(\初始值_out_21 ), .in1_22(\初始值_out_22 ),
    .in2_11(A_2_out_11), .in2_12(A_2_out_12), .in2_21(A_2_out_21), .in2_22(A_2_out_22), .in_9(init),
    .out_11(MUX_2_out_11), .out_12(MUX_2_out_12), .out_21(MUX_2_out_21), .out_22(MUX_2_out_22));
  \单位矩阵  \u_单位阵_2  (.out_11(\单位阵_2_out_11 ), .out_12(\单位阵_2_out_12 ), .out_21(\单位阵_2_out_21 ), .out_22(\单位阵_2_out_22 ));
  \矩阵选择  MUX_3 (
    .in1_11(\单位阵_2_out_11 ), .in1_12(\单位阵_2_out_12 ), .in1_21(\单位阵_2_out_21 ), .in1_22(\单位阵_2_out_22 ),
    .in2_11(S_A_out_11), .in2_12(S_A_out_12), .in2_21(S_A_out_21), .in2_22(S_A_out_22), .in_9(init),
    .out_11(MUX_3_out_11), .out_12(MUX_3_out_12), .out_21(MUX_3_out_21), .out_22(MUX_3_out_22));
  \寄存器矩阵  \u_矩阵A  (
    .in_11(MUX_2_out_11), .in_12(MUX_2_out_12), .in_21(MUX_2_out_21), .in_22(MUX_2_out_22), .ena(ena),
    .clk(clk), .clr(in_3), .out_11(a11), .out_12(a12), .out_21(a21), .out_22(a22));
  \寄存器矩阵  \u_矩阵S  (
    .in_11(MUX_3_out_11), .in_12(MUX_3_out_12), .in_21(MUX_3_out_21), .in_22(MUX_3_out_22), .ena(ena),
    .clk(clk), .clr(in_3), .out_11(s11), .out_12(s12), .out_21(s21), .out_22(s22));
  Multiplexer #(.width(32)) multiplexer_1 (.in0({32{1'b0}}), .in1(s12), .out(out_4), .sel(in_2));  // open: en

  // Other names for the same wires on the sheet: freeze = in_2; now = in_1; rst = in_3
endmodule

module \计数逻辑  (
  input  [31:0] \input ,
  input  in_2,
  output now,
  output freeze
);

  wire clk, comparator_1_eq, init;
  wire [31:0] multiplexer_1_out, shifter_1_out;
  wire [31:1] rst;

  Counter #(.width(1), .max('h1), .ongoal("stay")) counter_1 (
    .Q(init), .clk(clk), .clr(in_2));  // open: load, D, count, carry
  Clock clock_1 (.out(clk));
  Shifter #(.width(32), .shift("lr")) shifter_1 (.in({rst, now}), .\dist (5'b00001), .out(shifter_1_out));
  Comparator #(.width(32)) comparator_1 (.a({rst, now}), .b({32{1'b0}}), .eq(comparator_1_eq));  // open: gt, lt
  Multiplexer #(.width(32)) multiplexer_1 (
    .in0(\input ), .in1(shifter_1_out), .out(multiplexer_1_out), .sel(init));  // open: en
  Multiplexer multiplexer_2 (.in0(1'b0), .in1(comparator_1_eq), .out(freeze), .sel(init));  // open: en
  Register #(.width(32)) register_1 (.D(multiplexer_1_out), .Q({rst, now}), .clk(clk), .clr(in_2));  // open: en

  // Other names for the same wires on the sheet: clr = in_2; rst[0] = now
endmodule
