// Logisim project fsm.circ as structural Verilog: 3 circuits, main circuit fsm
module fsm (
  input  clr,
  input  [1:0] \input ,
  output \output 
);

  wire clk;
  wire [1:0] change_1_out, multiplexer_1_out, register_1_q;

  Clock clock_1 (.out(clk));
  change change_1 (.s(register_1_q), .in(\input ), .out(change_1_out));
  Multiplexer #(.width(2)) multiplexer_1 (
    .in0(change_1_out), .in1(2'b00), .out(multiplexer_1_out), .sel(clr));  // open: en
  Register #(.width(2)) register_1 (.D(multiplexer_1_out), .Q(register_1_q), .clk(clk));  // open: en, clr
  \output  output_1 (.s(register_1_q), .in(\input ), .out(\output ));
endmodule

module change (
  input  [1:0] s,
  input  [1:0] in,
  output [1:0] out
);

  wire not_1_out, not_2_out;

  and and_1 (out[1], s[0], not_1_out);
  not not_1 (not_1_out, in[0]);
  not not_2 (not_2_out, in[1]);
  and and_2 (out[0], not_2_out, in[0]);
endmodule

module \output  (
  input  [1:0] s,
  input  [1:0] in,
  output out
);

  wire not_1_out;

  and and_1 (out, s[1], not_1_out);
  not not_1 (not_1_out, in[0]);
endmodule
