// Logisim project ftoi.circ as structural Verilog: 1 circuit, main circuit ftoi
module ftoi (
  input  [15:0] in_1,
  output [31:0] out_2
);

  wire comparator_1_lt, comparator_2_eq, comparator_3_gt;
  wire [4:0] adder_1_out, exp, not_1_out;
  wire [15:0] multiplexer_3_out, out;
  wire [31:0] adder_2_out, multiplexer_1_out, multiplexer_2_out, multiplexer_4_out, not_2_out, shifter_1_out,
       shifter_2_out;

  Subtractor #(.width(5)) subtractor_1 (.a(in_1[14:10]), .b(5'b01111), .out(exp));  // open: bin, bout
  assign not_1_out = ~exp;  // NOT_Gate not_1, 5 bits wide
  Adder #(.width(5)) adder_1 (.a(not_1_out), .b(5'b00001), .out(adder_1_out));  // open: cin, cout
  assign not_2_out = ~{{16{1'b0}}, out};  // NOT_Gate not_2, 32 bits wide
  Shifter #(.width(32), .shift("lr")) shifter_1 (
    .in({16'h1, in_1[9:0], {6{1'b0}}}), .\dist (adder_1_out), .out(shifter_1_out));
  Adder #(.width(32)) adder_2 (.a(not_2_out), .b(32'h1), .out(adder_2_out));  // open: cin, cout
  Multiplexer #(.width(32)) multiplexer_1 (
    .in0({32{1'b0}}), .in1({32{1'b1}}), .out(multiplexer_1_out), .sel(in_1[15]));  // open: en
  Shifter #(.width(32)) shifter_2 (.in({16'h1, in_1[9:0], {6{1'b0}}}), .\dist (exp), .out(shifter_2_out));
  Comparator #(.width(5)) comparator_1 (.a(exp), .b({5{1'b0}}), .lt(comparator_1_lt));  // open: gt, eq
  Multiplexer #(.width(32)) multiplexer_2 (
    .in0({{16{1'b0}}, out}), .in1(adder_2_out), .out(multiplexer_2_out), .sel(in_1[15]));  // open: en
  Comparator #(.width(5), .mode("unsigned")) comparator_2 (
    .a({5{1'b0}}), .b(in_1[14:10]), .eq(comparator_2_eq));  // open: gt, lt
  Multiplexer #(.width(32)) multiplexer_3 (
    .in0(shifter_2_out), .in1(shifter_1_out), .out({out, multiplexer_3_out}), .sel(comparator_1_lt));  // open: en
  Multiplexer #(.width(32)) multiplexer_4 (
    .in0(multiplexer_2_out), .in1(multiplexer_1_out), .out(multiplexer_4_out), .sel(comparator_2_eq));  // open: en
  Multiplexer #(.width(32)) multiplexer_5 (
    .in0({32{1'b0}}), .in1(multiplexer_4_out), .out(out_2), .sel(comparator_3_gt));  // open: en
  Comparator #(.width(5), .mode("unsigned")) comparator_3 (
    .a({5{1'b1}}), .b(in_1[14:10]), .gt(comparator_3_gt));  // open: eq, lt

  // Other names for the same wires on the sheet: ex[4:0] = in_1[14:10]; frac[15:6] = in_1[9:0]; sign = in_1[15]
endmodule
