// Logisim project navigation.circ as structural Verilog: 3 circuits, main circuit navigation
module navigation (
  input  [1:0] dir,
  input  clk,
  input  rst,
  output arrive,
  output hit
);

  wire \状态存储_1_out_8 , \状态转移_1_arrive_2 , \状态转移_1_hit , \状态转移_1_ox ;
  wire [1:0] \状态存储_1_out_7 , \状态转移_1_oy ;

  \状态转移  \u_状态转移_1  (
    .dir(dir), .y(\状态存储_1_out_7 ), .x(\状态存储_1_out_8 ), .arrive(arrive), .oy(\状态转移_1_oy ), .ox(\状态转移_1_ox ),
    .arrive_2(\状态转移_1_arrive_2 ), .hit(\状态转移_1_hit ));
  \状态存储  \u_状态存储_1  (
    .in_1(\状态转移_1_oy ), .in_2(\状态转移_1_ox ), .in_3(\状态转移_1_arrive_2 ), .in_4(\状态转移_1_hit ), .in_5(clk),
    .in_6(rst), .out_7(\状态存储_1_out_7 ), .out_8(\状态存储_1_out_8 ), .out_9(arrive), .out_10(hit));
endmodule

module \状态存储  (
  input  [1:0] in_1,
  input  in_2,
  input  in_3,
  input  in_4,
  input  in_5,
  input  in_6,
  output [1:0] out_7,
  output out_8,
  output out_9,
  output out_10
);

  Register #(.width(2)) register_1 (.D(in_1), .Q(out_7), .clk(in_5), .clr(in_6));  // open: en
  Register #(.width(1)) register_2 (.D(in_2), .Q(out_8), .clk(in_5), .clr(in_6));  // open: en
  Register #(.width(1)) register_3 (.D(in_3), .Q(out_9), .clk(in_5), .clr(in_6));  // open: en
  Register #(.width(1)) register_4 (.D(in_4), .Q(out_10), .clk(in_5), .clr(in_6));  // open: en

  // Other names for the same wires on the sheet: clk = in_5; rst = in_6
endmodule

module \状态转移  (
  input  [1:0] dir,
  input  [1:0] y,
  input  x,
  input  arrive,
  output [1:0] oy,
  output ox,
  output arrive_2,
  output hit
);

  wire and_1_out, and_2_out, and_3_out, and_4_out, and_5_out, and_6_out, and_7_out, arrive_t,
       comparator_2_eq, comparator_2_gt, comparator_3_eq, comparator_4_eq, comparator_5_eq, comparator_6_eq,
       comparator_7_eq, comparator_8_eq, comparator_9_eq, dx, hitx, hity, multiplexer_2_out,
       multiplexer_6_out, multiplexer_9_out, nor_1_out, not_2_out, not_3_out, or_3_out;
  wire [1:0] adder_1_out, dy, multiplexer_1_out, multiplexer_5_out;

  not not_1 (arrive_t, arrive);
  Comparator #(.width(2), .mode("unsigned")) comparator_1 (.a(y), .b(2'b00));  // open: gt, eq, lt
  not not_2 (not_2_out, x);
  Comparator #(.width(2), .mode("unsigned")) comparator_2 (
    .a(y), .b(2'b00), .gt(comparator_2_gt), .eq(comparator_2_eq));  // open: lt
  Comparator #(.width(2), .mode("unsigned")) comparator_3 (.a(y), .b(2'b10), .eq(comparator_3_eq));  // open: gt, lt
  Comparator #(.width(2), .mode("unsigned")) comparator_4 (.a(dy), .b(2'b01), .eq(comparator_4_eq));  // open: gt, lt
  Comparator #(.width(2), .mode("unsigned")) comparator_5 (.a(y), .b(2'b00), .eq(comparator_5_eq));  // open: gt, lt
  Comparator #(.width(2), .mode("unsigned")) comparator_6 (.a(dy), .b(2'b11), .eq(comparator_6_eq));  // open: gt, lt
  not not_3 (not_3_out, x);
  Comparator #(.width(2), .mode("unsigned")) comparator_7 (.a(y), .b(2'b01), .eq(comparator_7_eq));  // open: gt, lt
  Comparator #(.width(2), .mode("unsigned")) comparator_8 (.a(dy), .b(2'b11), .eq(comparator_8_eq));  // open: gt, lt
  and and_1 (and_1_out, x, dx, comparator_2_gt);
  and and_2 (and_2_out, not_2_out, comparator_2_eq, dir[0]);
  Multiplexer #(.width(2)) multiplexer_1 (.in0(2'b01), .in1(2'b11), .out(multiplexer_1_out), .sel(dir[1]));  // open: en
  Multiplexer multiplexer_2 (.in0(1'b1), .in1(1'b0), .out(multiplexer_2_out), .sel(dir[1]));  // open: en
  and and_3 (and_3_out, comparator_3_eq, comparator_4_eq);
  or or_1 (hity, and_3_out, and_4_out, and_5_out);
  and and_4 (and_4_out, comparator_5_eq, comparator_6_eq, not_3_out);
  and and_5 (and_5_out, x, comparator_7_eq, comparator_8_eq);
  and and_6 (and_6_out, dir[0], nor_1_out);
  nor nor_1 (nor_1_out, x, dx);
  Multiplexer #(.width(2)) multiplexer_3 (.in0(multiplexer_1_out), .in1(2'b00), .out(dy), .sel(dir[0]));  // open: en
  Multiplexer multiplexer_4 (.in0(1'b0), .in1(multiplexer_2_out), .out(dx), .sel(dir[0]));  // open: en
  or or_2 (hitx, and_6_out, and_1_out, and_2_out);
  Adder #(.width(2)) adder_1 (.a(y), .b(dy), .out(adder_1_out));  // open: cin, cout
  Comparator #(.width(2), .mode("unsigned")) comparator_9 (.a(oy), .b(2'b10), .eq(comparator_9_eq));  // open: gt, lt
  Multiplexer #(.width(2)) multiplexer_5 (.in0(adder_1_out), .in1(y), .out(multiplexer_5_out), .sel(hity));  // open: en
  Multiplexer multiplexer_6 (.in0(dx), .in1(x), .out(multiplexer_6_out), .sel(hitx));  // open: en
  and and_7 (and_7_out, comparator_9_eq, ox);
  Multiplexer #(.width(2)) multiplexer_7 (.in0(2'b00), .in1(multiplexer_5_out), .out(oy), .sel(arrive_t));  // open: en
  Multiplexer multiplexer_8 (.in0(1'b0), .in1(multiplexer_9_out), .out(ox), .sel(arrive_t));  // open: en
  Multiplexer multiplexer_9 (.in0(x), .in1(multiplexer_6_out), .out(multiplexer_9_out), .sel(dir[0]));  // open: en
  Multiplexer multiplexer_10 (.in0(1'b0), .in1(and_7_out), .out(arrive_2), .sel(arrive_t));  // open: en
  or or_3 (or_3_out, hity, hitx);
  Multiplexer multiplexer_11 (.in0(1'b0), .in1(or_3_out), .out(hit), .sel(arrive_t));  // open: en

  // Other names for the same wires on the sheet: ax = ox; ay[1:0] = oy; d0 = dir[0]; d1 = dir[1]
endmodule
