// Logisim project swap.circ as structural Verilog: 1 circuit, main circuit swap
module swap (
  input  I1,
  input  I2,
  input  S,
  output O1,
  output O2
);

  wire I1_nS_out, I1_S_out, I2_nS_out, I2_S_out, not_1_out;

  not not_1 (not_1_out, S);
  and I1_S (I1_S_out, I1, S);
  and I2_S (I2_S_out, I2, S);
  and I1_nS (I1_nS_out, I1, not_1_out);
  and I2_nS (I2_nS_out, I2, not_1_out);
  or or_1 (O1, I2_S_out, I1_nS_out);
  or or_2 (O2, I1_S_out, I2_nS_out);
endmodule
